# Fritzing sketch ESP32 Soccer Bot PCB (saved by Fritzing 0.9.4)
breadboards: 1

parts:
  VCC1 = Battery
  J3 = female pin header, 5 pins [form="♀ (female)"]
  J4 = female pin header, 5 pins [form="♀ (female)"]
  J5 = female pin header, 5 pins [form="♀ (female)"]
  J2 = female pin header, 15 pins [form="♀ (female)"]  # not connected
  J6 = female pin header, 15 pins [form="♀ (female)"]  # not connected
  J1 = female pin header, 15 pins [form="♀ (female)"]  # not connected
  J7 = female pin header, 15 pins [form="♀ (female)"]  # not connected

nets:
  N1: VCC1.+, J3.pin1, J3.pin2, J3.pin3, J3.pin4, J3.pin5
  N2: J4.pin1, J4.pin2, J4.pin3, J4.pin4, J4.pin5
  N3: J5.pin1, J5.pin2, J5.pin3, J5.pin4, J5.pin5
